# Fritzing sketch TA (saved by Fritzing 0.9.3b)
breadboards: 2

parts:
  U1 = ESP8266 NodeMCU LoLin module
  hc-sr1 = hc-sr04
  LED1 = smd LED [color="Green (555nm)" package="1206 [SMD]"]
  R1 = Resistor [tolerance=±5% resistance=220 package="0402 [SMD]"]

nets:
  N1: U1.D0, R1.Pin_1
  GND: U1.GND, hc-sr1.GND, LED1.anode
  N2: U1.D5, hc-sr1.Echo
  N3: U1.D6, hc-sr1.Trig
  VIN: U1.Vin, hc-sr1.VCC
  N4: LED1.cathode, R1.Pin_0

custom parts:
  ESP8266 NodeMCU LoLin module: ESP8266 based NodeMCU
